// Logisim project prova1.circ as structural Verilog: 7 circuits, main circuit main
module main (
  input  _1,
  input  _2,
  input  _4,
  input  _1_2,
  input  _2_2,
  input  _4_2,
  input  _8,
  output _1_3,
  output _2_3,
  output _4_3,
  output _8_2,
  output _16,
  output _32,
  output _64
);

  wire multiplicador_4_a___b, multiplicador_5_a___b, multiplicador_6_a___b, multiplicador_7_a___b,
       multiplicador_8_a___b, multiplicador_9_a___b, multiplicador_10_a___b, multiplicador_11_a___b;
  wire [0:0] multiplicador_1_a___b, multiplicador_2_a___b, multiplicador_3_a___b, multiplicador_12_a___b;
  wire [1:0] somador_completo_1_bit0, somador_completo_2_bit0, somador_completo_3_bit0;
  wire [1:1] ula_4bits_3_result_2, ula_4bits_4_result_2, ula_4bits_5_result_2, ula_4bits_6_result_2;
  wire [3:1] ula_4bits_1_result, ula_4bits_2_result, ula_4bits_3_result, ula_4bits_4_result,
       ula_4bits_5_result, ula_4bits_6_result, ula_4bits_7_result;

  Multiplicador multiplicador_1 (.a(_1), .b(_1_2), .a___b(multiplicador_1_a___b[0]));
  Multiplicador multiplicador_2 (.a(_1_2), .b(_2), .a___b(multiplicador_2_a___b[0]));
  Multiplicador multiplicador_3 (.a(_2_2), .b(_1), .a___b(multiplicador_3_a___b[0]));
  Multiplicador multiplicador_4 (.a(_1_2), .b(_4), .a___b(multiplicador_4_a___b));
  Multiplicador multiplicador_5 (.a(_2_2), .b(_2), .a___b(multiplicador_5_a___b));
  Multiplicador multiplicador_6 (.a(_4_2), .b(_1), .a___b(multiplicador_6_a___b));
  Multiplicador multiplicador_7 (.a(_2_2), .b(_4), .a___b(multiplicador_7_a___b));
  Multiplicador multiplicador_8 (.a(_4_2), .b(_2), .a___b(multiplicador_8_a___b));
  Multiplicador multiplicador_9 (.a(_8), .b(_1), .a___b(multiplicador_9_a___b));
  Multiplicador multiplicador_10 (.a(_4_2), .b(_4), .a___b(multiplicador_10_a___b));
  Multiplicador multiplicador_11 (.a(_8), .b(_2), .a___b(multiplicador_11_a___b));
  Multiplicador multiplicador_12 (.a(_8), .b(_4), .a___b(multiplicador_12_a___b[0]));
  Somador_completo somador_completo_1 (
    .a(multiplicador_4_a___b), .b(multiplicador_5_a___b), .received(multiplicador_6_a___b),
    .send_bit(somador_completo_1_bit0[1]), .bit0(somador_completo_1_bit0[0]));
  Somador_completo somador_completo_2 (
    .a(multiplicador_7_a___b), .b(multiplicador_8_a___b), .received(multiplicador_9_a___b),
    .send_bit(somador_completo_2_bit0[1]), .bit0(somador_completo_2_bit0[0]));
  Somador_completo somador_completo_3 (
    .a(1'b0), .b(multiplicador_10_a___b), .received(multiplicador_11_a___b),
    .send_bit(somador_completo_3_bit0[1]), .bit0(somador_completo_3_bit0[0]));
  ULA_4bits ula_4bits_1 (
    .a({3'b000, multiplicador_1_a___b[0]}), .b(4'b0000), .b_invert(1'b0), .carry_in(1'b0), .op_code(2'b11),
    .result({ula_4bits_1_result, _1_3}));  // open: carry_out
  ULA_4bits ula_4bits_2 (
    .a({3'b000, multiplicador_2_a___b[0]}), .b({3'b000, multiplicador_3_a___b[0]}), .b_invert(1'b0),
    .carry_in(ula_4bits_1_result[1]), .op_code(2'b11), .result({ula_4bits_2_result, _2_3}));  // open: carry_out
  ULA_4bits ula_4bits_3 (
    .a({2'b00, somador_completo_1_bit0}), .b(4'b0000), .b_invert(1'b0), .carry_in(ula_4bits_2_result[1]),
    .op_code(2'b11), .result({ula_4bits_3_result[3], ula_4bits_3_result_2[1], ula_4bits_3_result[1], _4_3}));  // open: carry_out
  ULA_4bits ula_4bits_4 (
    .a({2'b00, somador_completo_2_bit0}), .b({2'b00, ula_4bits_3_result_2[1], 1'b0}), .b_invert(1'b0),
    .carry_in(ula_4bits_3_result[1]), .op_code(2'b11),
    .result({ula_4bits_4_result[3], ula_4bits_4_result_2[1], ula_4bits_4_result[1], _8_2}));  // open: carry_out
  ULA_4bits ula_4bits_5 (
    .a({2'b00, somador_completo_3_bit0}), .b({2'b00, ula_4bits_4_result_2[1], 1'b0}), .b_invert(1'b0),
    .carry_in(ula_4bits_4_result[1]), .op_code(2'b11),
    .result({ula_4bits_5_result[3], ula_4bits_5_result_2[1], ula_4bits_5_result[1], _16}));  // open: carry_out
  ULA_4bits ula_4bits_6 (
    .a({3'b000, multiplicador_12_a___b[0]}), .b({2'b00, ula_4bits_5_result_2[1], 1'b0}), .b_invert(1'b0),
    .carry_in(ula_4bits_5_result[1]), .op_code(2'b11),
    .result({ula_4bits_6_result[3], ula_4bits_6_result_2[1], ula_4bits_6_result[1], _32}));  // open: carry_out
  ULA_4bits ula_4bits_7 (
    .a(4'b0000), .b({2'b00, ula_4bits_6_result_2[1], 1'b0}), .b_invert(1'b0),
    .carry_in(ula_4bits_6_result[1]), .op_code(2'b11), .result({ula_4bits_7_result, _64}));  // open: carry_out
endmodule

module Meio_somador (
  input  a,
  input  b,
  output send_bit,
  output bit0
);

  and and_1 (send_bit, a, b);
  xor xor_1 (bit0, a, b);

  // Notes on the sheet:
  //   a + b = send_bit bit0
  //   0 + 0 = 0             0
  //   0 + 1 = 0             1
  //   1 + 0 = 0             1
  //   1 + 1 = 1             0
endmodule

module Somador_completo (
  input  a,
  input  b,
  input  received,
  output send_bit,
  output bit0
);

  wire meio_somador_1_bit0, meio_somador_1_send_bit, meio_somador_3_send_bit;

  Meio_somador meio_somador_1 (.a(b), .b(a), .send_bit(meio_somador_1_send_bit), .bit0(meio_somador_1_bit0));
  Meio_somador meio_somador_2 (
    .a(meio_somador_3_send_bit), .b(meio_somador_1_send_bit), .bit0(send_bit));  // open: send_bit
  Meio_somador meio_somador_3 (.a(received), .b(meio_somador_1_bit0), .send_bit(meio_somador_3_send_bit), .bit0(bit0));

  // Notes on the sheet:
  //   a + b + received = send_bit  bit0
  //   0 + 0 +           0  = 0               0
  //   0 + 1 +           0  = 0               1
  //   1 + 0 +           0  = 0               1
  //   1 + 1 +           0  = 1               0
  //   0 + 0 +           1  = 0               1
  //   0 + 1 +           1  = 1               0
  //   1 + 0 +           1  = 1               0
  //   1 + 1 +           1  = 1               1
endmodule

module ULA_1bit (
  input  b_invert,
  input  carry_in,
  input  a,
  input  b,
  input  [1:0] op_code,
  output carry_out,
  output result
);

  wire and_1_out, multiplexer_1_out, not_1_out, not_2_out, or_1_out, somador_completo_1_bit0;

  not not_1 (not_1_out, b);
  Multiplexer #(.enable("false")) multiplexer_1 (.in0(b), .in1(not_1_out), .out(multiplexer_1_out), .sel(b_invert));
  and and_1 (and_1_out, a, b);
  or or_1 (or_1_out, a, b);
  not not_2 (not_2_out, a);
  Somador_completo somador_completo_1 (
    .a(a), .b(multiplexer_1_out), .received(carry_in), .send_bit(carry_out), .bit0(somador_completo_1_bit0));
  Multiplexer #(.select(2), .enable("false")) multiplexer_2 (
    .in0(and_1_out), .in1(or_1_out), .in2(not_2_out), .in3(somador_completo_1_bit0), .out(result),
    .sel(op_code));

  // Notes on the sheet:
  //   op code -> op
  //   00 -> and(a, b)
  //   01 -> or(a, b)
  //   10 -> not(a)
  //   11 -> a + b
endmodule

module ULA_4bits (
  input  b_invert,
  input  carry_in,
  input  [3:0] a,
  input  [3:0] b,
  input  [1:0] op_code,
  output carry_out,
  output [3:0] result
);

  wire ula_1bit_1_carry_out, ula_1bit_2_carry_out, ula_1bit_3_carry_out;

  ULA_1bit ula_1bit_1 (
    .a(a[0]), .b(b[0]), .b_invert(b_invert), .carry_in(carry_in), .op_code(op_code),
    .carry_out(ula_1bit_1_carry_out), .result(result[0]));
  ULA_1bit ula_1bit_2 (
    .a(a[1]), .b(b[1]), .b_invert(b_invert), .carry_in(ula_1bit_1_carry_out), .op_code(op_code),
    .carry_out(ula_1bit_2_carry_out), .result(result[1]));
  ULA_1bit ula_1bit_3 (
    .a(a[2]), .b(b[2]), .b_invert(b_invert), .carry_in(ula_1bit_2_carry_out), .op_code(op_code),
    .carry_out(ula_1bit_3_carry_out), .result(result[2]));
  ULA_1bit ula_1bit_4 (
    .a(a[3]), .b(b[3]), .b_invert(b_invert), .carry_in(ula_1bit_3_carry_out), .op_code(op_code),
    .carry_out(carry_out), .result(result[3]));
endmodule

module Multiplicador (
  input  a,
  input  b,
  output a___b
);

  and and_1 (a___b, a, b);
endmodule

module PROVA1 (
  input  [2:0] in_1,
  input  [3:0] in_2,
  output [7:0] out_3
);

  main main_1 (
    ._1(in_1[0]), ._2(in_1[1]), ._4(in_1[2]), ._1_2(in_2[0]), ._2_2(in_2[1]), ._4_2(in_2[2]), ._8(in_2[3]),
    ._1_3(out_3[0]), ._2_3(out_3[1]), ._4_3(out_3[2]), ._8_2(out_3[3]), ._16(out_3[4]), ._32(out_3[5]),
    ._64(out_3[6]));

  assign out_3[7] = 1'b0;
endmodule
