// Logisim project ULA 4bits (and bit-bit, or bit-bit, not, sum, subtract).circ as structural Verilog: 1 circuit, main circuit main
module main (
  input  b_invert,
  input  [3:0] a,
  input  [3:0] b,
  input  [1:0] op_code,
  output carry_out,
  output [3:0] result
);

  wire bit0_carry_out, bit1_carry_out, bit2_carry_out;

  ULA_1bit__and__or__not__sum__subtract__main bit0 (
    .a(a[0]), .b(b[0]), .b_invert(b_invert), .carry_in(b_invert), .op_code(op_code),
    .carry_out(bit0_carry_out), .result(result[0]));
  ULA_1bit__and__or__not__sum__subtract__main bit1 (
    .a(a[1]), .b(b[1]), .b_invert(b_invert), .carry_in(bit0_carry_out), .op_code(op_code),
    .carry_out(bit1_carry_out), .result(result[1]));
  ULA_1bit__and__or__not__sum__subtract__main bit2 (
    .a(a[2]), .b(b[2]), .b_invert(b_invert), .carry_in(bit1_carry_out), .op_code(op_code),
    .carry_out(bit2_carry_out), .result(result[2]));
  ULA_1bit__and__or__not__sum__subtract__main bit3 (
    .a(a[3]), .b(b[3]), .b_invert(b_invert), .carry_in(bit2_carry_out), .op_code(op_code),
    .carry_out(carry_out), .result(result[3]));
endmodule
