// Logisim project ALU 4 bits - Logisim.circ as structural Verilog: 1 circuit, main circuit main
module main (
  input  [3:0] a,
  input  [3:0] b,
  input  [3:0] op_code,
  output [3:0] out_4
);

  wire [3:0] and_1_out, and_2_out, and_3_out, nand_1_out, nor_1_out, not_1_out, not_2_out, or_1_out,
       or_2_out, or_3_out, xnor_1_out, xor_1_out;

  assign not_1_out = ~a;  // NOT_Gate not_1, 4 bits wide
  assign not_2_out = ~b;  // NOT_Gate not_2, 4 bits wide
  assign nor_1_out = ~(a | b);  // NOR_Gate nor_1, 4 bits wide
  assign and_1_out = not_1_out & b;  // AND_Gate and_1, 4 bits wide
  assign nand_1_out = ~(a & b);  // NAND_Gate nand_1, 4 bits wide
  assign xor_1_out = a ^ b;  // XOR_Gate xor_1, 4 bits wide
  assign and_2_out = a & not_2_out;  // AND_Gate and_2, 4 bits wide
  assign or_1_out = not_1_out | b;  // OR_Gate or_1, 4 bits wide
  assign xnor_1_out = ~(a ^ b);  // XNOR_Gate xnor_1, 4 bits wide
  assign and_3_out = a & b;  // AND_Gate and_3, 4 bits wide
  assign or_2_out = a | not_2_out;  // OR_Gate or_2, 4 bits wide
  assign or_3_out = a | b;  // OR_Gate or_3, 4 bits wide
  Multiplexer #(.select(4), .width(4), .enable("false")) multiplexer_1 (
    .in0(not_1_out), .in1(nor_1_out), .in2(and_1_out), .in3(4'b0000), .in4(nand_1_out), .in5(not_2_out),
    .in6(xor_1_out), .in7(and_2_out), .in8(or_1_out), .in9(xnor_1_out), .in10(b), .in11(and_3_out),
    .in12(4'b1111), .in13(or_2_out), .in14(or_3_out), .in15(a), .out(out_4), .sel(op_code));
endmodule
