// Logisim project Somador_completo_4bits.circ as structural Verilog: 1 circuit, main circuit main
module main (
  input  [3:0] a,
  input  [3:0] b,
  input  received_bit,
  output [3:0] a___b,
  output send_bit
);

  wire bit1_send_bit, bit2_send_bit, bit3_send_bit;

  Somador_completo_a_mais_b_mais_bit_recebido_main bit3 (
    .a(a[3]), .b(b[3]), .received(received_bit), .send_bit(bit3_send_bit), .bit0(a___b[3]));
  Somador_completo_a_mais_b_mais_bit_recebido_main bit2 (
    .a(a[2]), .b(b[2]), .received(bit3_send_bit), .send_bit(bit2_send_bit), .bit0(a___b[2]));
  Somador_completo_a_mais_b_mais_bit_recebido_main bit1 (
    .a(a[1]), .b(b[1]), .received(bit2_send_bit), .send_bit(bit1_send_bit), .bit0(a___b[1]));
  Somador_completo_a_mais_b_mais_bit_recebido_main bit0 (
    .a(a[0]), .b(b[0]), .received(bit1_send_bit), .send_bit(send_bit), .bit0(a___b[0]));
endmodule
