// Logisim project Somador_completo_8bits.circ as structural Verilog: 1 circuit, main circuit main
module main (
  input  [7:0] a,
  input  [7:0] b,
  input  received_bit,
  output [7:0] a___b,
  output send_bit
);

  wire main_1_send_bit, main_2_send_bit, main_3_send_bit, main_4_send_bit, main_5_send_bit, main_6_send_bit,
       main_7_send_bit;

  Somador_completo_a_mais_b_mais_bit_recebido_main main_1 (
    .a(a[0]), .b(b[0]), .received(received_bit), .send_bit(main_1_send_bit), .bit0(a___b[0]));
  Somador_completo_a_mais_b_mais_bit_recebido_main main_2 (
    .a(a[1]), .b(b[1]), .received(main_1_send_bit), .send_bit(main_2_send_bit), .bit0(a___b[1]));
  Somador_completo_a_mais_b_mais_bit_recebido_main main_3 (
    .a(a[2]), .b(b[2]), .received(main_2_send_bit), .send_bit(main_3_send_bit), .bit0(a___b[2]));
  Somador_completo_a_mais_b_mais_bit_recebido_main main_4 (
    .a(a[3]), .b(b[3]), .received(main_3_send_bit), .send_bit(main_4_send_bit), .bit0(a___b[3]));
  Somador_completo_a_mais_b_mais_bit_recebido_main main_5 (
    .a(a[4]), .b(b[4]), .received(main_4_send_bit), .send_bit(main_5_send_bit), .bit0(a___b[4]));
  Somador_completo_a_mais_b_mais_bit_recebido_main main_6 (
    .a(a[5]), .b(b[5]), .received(main_5_send_bit), .send_bit(main_6_send_bit), .bit0(a___b[5]));
  Somador_completo_a_mais_b_mais_bit_recebido_main main_7 (
    .a(a[6]), .b(b[6]), .received(main_6_send_bit), .send_bit(main_7_send_bit), .bit0(a___b[6]));
  Somador_completo_a_mais_b_mais_bit_recebido_main main_8 (
    .a(a[7]), .b(b[7]), .received(main_7_send_bit), .send_bit(send_bit), .bit0(a___b[7]));
endmodule
