// Logisim project Somador 4bits CLA.circ as structural Verilog
module Somador_4bits_CLA (
  input  C_in,
  input  A4,
  input  A3,
  input  A2,
  input  A1,
  input  B4,
  input  B3,
  input  B2,
  input  B1,
  output Soma4,
  output Soma3,
  output Soma2,
  output Soma1,
  output C_out
);

  wire and_1_out, and_2_out, and_3_out, and_4_out, and_5_out, and_6_out, and_7_out, and_8_out, and_9_out,
       and_10_out, and_11_out, and_12_out, and_13_out, and_14_out, and_15_out, and_16_out, and_17_out,
       and_18_out, and_19_out, and_20_out, and_21_out, and_22_out, and_23_out, and_24_out, and_25_out,
       and_26_out, and_27_out, and_28_out, and_29_out, and_30_out, and_31_out, and_32_out, and_33_out,
       and_34_out, and_35_out, and_36_out, and_37_out, and_38_out, and_39_out, and_40_out, and_41_out,
       and_42_out, and_43_out, and_44_out, and_45_out, and_46_out, and_47_out, and_48_out, and_49_out,
       and_50_out, and_51_out, and_52_out, and_53_out, and_54_out, and_55_out, and_56_out, and_57_out,
       and_58_out, and_59_out, and_60_out, and_61_out, and_62_out, and_63_out, and_64_out, and_65_out,
       and_66_out, and_67_out, and_68_out, and_69_out, and_70_out, and_71_out, and_72_out, and_73_out,
       and_74_out, and_75_out, and_76_out, and_77_out, and_78_out, and_79_out, and_80_out, and_81_out,
       and_82_out, and_83_out, and_84_out, and_85_out, and_86_out, and_87_out, and_88_out, and_89_out,
       and_90_out, and_91_out, and_92_out, and_93_out, and_94_out, and_95_out, and_96_out, and_97_out,
       and_98_out, and_99_out, and_100_out, and_101_out, and_102_out, and_103_out, and_104_out, and_105_out,
       and_106_out, and_107_out, and_108_out, and_109_out, and_110_out, and_111_out, and_112_out,
       and_113_out, and_114_out, and_115_out, and_116_out, and_117_out, and_118_out, and_119_out,
       and_120_out, and_121_out, and_122_out, and_123_out, and_124_out, and_125_out, and_126_out,
       and_127_out, not_1_out, not_2_out, not_3_out, not_4_out, not_5_out, not_6_out, not_7_out, not_8_out,
       not_9_out, not_10_out, not_11_out, not_12_out, not_13_out, not_14_out, not_15_out, not_16_out,
       not_17_out, not_18_out, not_19_out, not_20_out, not_21_out, not_22_out, not_23_out, not_24_out,
       not_25_out, not_26_out, not_27_out, not_28_out, not_29_out, not_30_out, not_31_out, not_32_out,
       not_33_out, not_34_out, not_35_out, not_36_out, not_37_out, not_38_out, not_39_out, not_40_out,
       not_41_out, not_42_out, not_43_out, not_44_out, not_45_out, not_46_out, not_47_out, not_48_out,
       not_49_out, not_50_out, not_51_out, not_52_out, not_53_out, not_54_out, not_55_out, not_56_out,
       not_57_out, not_58_out, not_59_out, not_60_out, not_61_out, not_62_out, not_63_out, not_64_out,
       not_65_out, not_66_out, not_67_out, not_68_out, not_69_out, not_70_out, not_71_out, not_72_out,
       not_73_out, not_74_out, not_75_out, not_76_out, not_77_out, not_78_out, not_79_out, not_80_out,
       not_81_out, not_82_out, not_83_out, not_84_out, not_85_out, not_86_out, not_87_out, not_88_out,
       not_89_out, not_90_out, not_91_out, not_92_out, not_93_out, not_94_out, not_95_out, not_96_out,
       not_97_out, not_98_out, not_99_out, not_100_out, not_101_out, not_102_out, not_103_out, not_104_out,
       not_105_out, not_106_out, not_107_out, not_108_out, not_109_out, not_110_out, not_111_out,
       not_112_out, not_113_out, not_114_out, not_115_out, not_116_out, not_117_out, not_118_out,
       not_119_out, not_120_out, not_121_out, not_122_out, not_123_out, not_124_out, not_125_out,
       not_126_out, not_127_out, not_128_out, not_129_out, not_130_out, not_131_out, not_132_out,
       not_133_out, not_134_out, not_135_out, not_136_out, not_137_out, not_138_out, not_139_out,
       not_140_out, not_141_out, not_142_out, not_143_out, not_144_out, not_145_out, not_146_out,
       not_147_out, not_148_out, not_149_out, not_150_out, not_151_out, not_152_out, not_153_out,
       not_154_out, not_155_out, not_156_out, not_157_out, not_158_out, not_159_out, not_160_out,
       not_161_out, not_162_out, not_163_out, not_164_out, not_165_out, not_166_out, not_167_out,
       not_168_out, not_169_out, not_170_out, not_171_out, not_172_out, not_173_out, not_174_out,
       not_175_out, not_176_out, not_177_out, not_178_out, not_179_out, not_180_out, not_181_out,
       not_182_out, not_183_out, not_184_out, not_185_out, not_186_out, not_187_out, not_188_out,
       not_189_out, not_190_out, not_191_out, not_192_out, not_193_out, not_194_out, not_195_out,
       not_196_out, not_197_out, not_198_out, not_199_out, not_200_out, not_201_out, not_202_out,
       not_203_out, not_204_out, not_205_out, not_206_out, not_207_out, not_208_out, not_209_out,
       not_210_out, not_211_out, not_212_out, not_213_out, not_214_out, not_215_out, not_216_out,
       not_217_out, not_218_out, not_219_out, not_220_out, not_221_out, not_222_out, not_223_out,
       not_224_out, not_225_out, not_226_out, not_227_out, not_228_out, not_229_out, not_230_out,
       not_231_out, not_232_out, not_233_out, not_234_out, not_235_out, not_236_out, not_237_out,
       not_238_out, not_239_out, not_240_out, not_241_out, not_242_out, not_243_out, not_244_out,
       not_245_out, not_246_out, not_247_out, not_248_out, not_249_out, not_250_out, not_251_out,
       not_252_out, not_253_out, not_254_out, or_4_out, or_5_out;

  not not_1 (not_1_out, C_in);
  not not_2 (not_2_out, A4);
  not not_3 (not_3_out, A3);
  not not_4 (not_4_out, A2);
  not not_5 (not_5_out, A1);
  not not_6 (not_6_out, C_in);
  not not_7 (not_7_out, A4);
  not not_8 (not_8_out, A3);
  not not_9 (not_9_out, A2);
  not not_10 (not_10_out, B1);
  not not_11 (not_11_out, C_in);
  not not_12 (not_12_out, A4);
  not not_13 (not_13_out, A3);
  not not_14 (not_14_out, A1);
  not not_15 (not_15_out, B2);
  not not_16 (not_16_out, C_in);
  not not_17 (not_17_out, A4);
  not not_18 (not_18_out, A3);
  not not_19 (not_19_out, B2);
  not not_20 (not_20_out, B1);
  not not_21 (not_21_out, C_in);
  not not_22 (not_22_out, A4);
  not not_23 (not_23_out, A2);
  not not_24 (not_24_out, A1);
  not not_25 (not_25_out, B3);
  not not_26 (not_26_out, C_in);
  not not_27 (not_27_out, A4);
  not not_28 (not_28_out, A2);
  not not_29 (not_29_out, B3);
  not not_30 (not_30_out, B1);
  not not_31 (not_31_out, C_in);
  not not_32 (not_32_out, A4);
  not not_33 (not_33_out, A1);
  not not_34 (not_34_out, B3);
  not not_35 (not_35_out, B2);
  not not_36 (not_36_out, C_in);
  not not_37 (not_37_out, A4);
  not not_38 (not_38_out, B3);
  not not_39 (not_39_out, B2);
  not not_40 (not_40_out, B1);
  not not_41 (not_41_out, A4);
  not not_42 (not_42_out, A3);
  not not_43 (not_43_out, A2);
  not not_44 (not_44_out, A1);
  not not_45 (not_45_out, B1);
  not not_46 (not_46_out, A4);
  not not_47 (not_47_out, A3);
  not not_48 (not_48_out, A2);
  not not_49 (not_49_out, B2);
  not not_50 (not_50_out, A4);
  not not_51 (not_51_out, A3);
  not not_52 (not_52_out, A1);
  not not_53 (not_53_out, B2);
  not not_54 (not_54_out, B1);
  not not_55 (not_55_out, A4);
  not not_56 (not_56_out, A3);
  not not_57 (not_57_out, B3);
  not not_58 (not_58_out, A4);
  not not_59 (not_59_out, A2);
  not not_60 (not_60_out, A1);
  not not_61 (not_61_out, B3);
  not not_62 (not_62_out, B1);
  not not_63 (not_63_out, A4);
  not not_64 (not_64_out, A2);
  not not_65 (not_65_out, B3);
  not not_66 (not_66_out, B2);
  not not_67 (not_67_out, A4);
  not not_68 (not_68_out, A1);
  not not_69 (not_69_out, B3);
  not not_70 (not_70_out, B2);
  not not_71 (not_71_out, B1);
  not not_72 (not_72_out, A4);
  not not_73 (not_73_out, B4);
  not not_74 (not_74_out, A4);
  not not_75 (not_75_out, B4);
  not not_76 (not_76_out, A4);
  not not_77 (not_77_out, B4);
  not not_78 (not_78_out, A4);
  not not_79 (not_79_out, B4);
  not not_80 (not_80_out, A4);
  not not_81 (not_81_out, B4);
  not not_82 (not_82_out, A4);
  not not_83 (not_83_out, B4);
  not not_84 (not_84_out, A4);
  not not_85 (not_85_out, B4);
  not not_86 (not_86_out, C_in);
  not not_87 (not_87_out, A3);
  not not_88 (not_88_out, A2);
  not not_89 (not_89_out, A1);
  not not_90 (not_90_out, B4);
  not not_91 (not_91_out, C_in);
  not not_92 (not_92_out, A3);
  not not_93 (not_93_out, A2);
  not not_94 (not_94_out, B4);
  not not_95 (not_95_out, B1);
  not not_96 (not_96_out, C_in);
  not not_97 (not_97_out, A3);
  not not_98 (not_98_out, A1);
  not not_99 (not_99_out, B4);
  not not_100 (not_100_out, B2);
  not not_101 (not_101_out, C_in);
  not not_102 (not_102_out, A3);
  not not_103 (not_103_out, B4);
  not not_104 (not_104_out, B2);
  not not_105 (not_105_out, B1);
  not not_106 (not_106_out, C_in);
  not not_107 (not_107_out, A2);
  not not_108 (not_108_out, A1);
  not not_109 (not_109_out, B4);
  not not_110 (not_110_out, B3);
  not not_111 (not_111_out, A3);
  not not_112 (not_112_out, A2);
  not not_113 (not_113_out, A1);
  not not_114 (not_114_out, B4);
  not not_115 (not_115_out, B1);
  not not_116 (not_116_out, A3);
  not not_117 (not_117_out, A2);
  not not_118 (not_118_out, B4);
  not not_119 (not_119_out, B2);
  not not_120 (not_120_out, A3);
  not not_121 (not_121_out, A1);
  not not_122 (not_122_out, B4);
  not not_123 (not_123_out, B2);
  not not_124 (not_124_out, B1);
  not not_125 (not_125_out, A3);
  not not_126 (not_126_out, B4);
  not not_127 (not_127_out, B3);
  not not_128 (not_128_out, A2);
  not not_129 (not_129_out, B4);
  not not_130 (not_130_out, B3);
  not not_131 (not_131_out, B2);
  not not_132 (not_132_out, A2);
  not not_133 (not_133_out, B4);
  not not_134 (not_134_out, B3);
  not not_135 (not_135_out, B1);
  not not_136 (not_136_out, A1);
  not not_137 (not_137_out, B4);
  not not_138 (not_138_out, B3);
  not not_139 (not_139_out, B2);
  not not_140 (not_140_out, B4);
  not not_141 (not_141_out, B3);
  not not_142 (not_142_out, B2);
  not not_143 (not_143_out, B1);
  not not_144 (not_144_out, A4);
  not not_145 (not_145_out, B4);
  not not_146 (not_146_out, A4);
  not not_147 (not_147_out, B4);
  not not_148 (not_148_out, A4);
  not not_149 (not_149_out, B4);
  not not_150 (not_150_out, A4);
  not not_151 (not_151_out, B4);
  not not_152 (not_152_out, A4);
  not not_153 (not_153_out, B4);
  not not_154 (not_154_out, B4);
  not not_155 (not_155_out, B4);
  not not_156 (not_156_out, B4);
  not not_157 (not_157_out, C_in);
  not not_158 (not_158_out, A3);
  not not_159 (not_159_out, A2);
  not not_160 (not_160_out, A1);
  not not_161 (not_161_out, C_in);
  not not_162 (not_162_out, A3);
  not not_163 (not_163_out, A2);
  not not_164 (not_164_out, B1);
  not not_165 (not_165_out, C_in);
  not not_166 (not_166_out, A3);
  not not_167 (not_167_out, A1);
  not not_168 (not_168_out, B2);
  not not_169 (not_169_out, C_in);
  not not_170 (not_170_out, A3);
  not not_171 (not_171_out, B2);
  not not_172 (not_172_out, B1);
  not not_173 (not_173_out, A3);
  not not_174 (not_174_out, A2);
  not not_175 (not_175_out, A1);
  not not_176 (not_176_out, B1);
  not not_177 (not_177_out, A3);
  not not_178 (not_178_out, A2);
  not not_179 (not_179_out, B2);
  not not_180 (not_180_out, A3);
  not not_181 (not_181_out, A1);
  not not_182 (not_182_out, B2);
  not not_183 (not_183_out, B1);
  not not_184 (not_184_out, A3);
  not not_185 (not_185_out, B3);
  not not_186 (not_186_out, A3);
  not not_187 (not_187_out, B3);
  not not_188 (not_188_out, A3);
  not not_189 (not_189_out, B3);
  not not_190 (not_190_out, C_in);
  not not_191 (not_191_out, A2);
  not not_192 (not_192_out, A1);
  not not_193 (not_193_out, B3);
  not not_194 (not_194_out, C_in);
  not not_195 (not_195_out, A2);
  not not_196 (not_196_out, B3);
  not not_197 (not_197_out, B1);
  not not_198 (not_198_out, C_in);
  not not_199 (not_199_out, A1);
  not not_200 (not_200_out, B3);
  not not_201 (not_201_out, B2);
  not not_202 (not_202_out, C_in);
  not not_203 (not_203_out, B3);
  not not_204 (not_204_out, B2);
  not not_205 (not_205_out, B1);
  not not_206 (not_206_out, A2);
  not not_207 (not_207_out, A1);
  not not_208 (not_208_out, B3);
  not not_209 (not_209_out, B1);
  not not_210 (not_210_out, A2);
  not not_211 (not_211_out, B3);
  not not_212 (not_212_out, B2);
  not not_213 (not_213_out, A1);
  not not_214 (not_214_out, B3);
  not not_215 (not_215_out, B2);
  not not_216 (not_216_out, B1);
  not not_217 (not_217_out, A3);
  not not_218 (not_218_out, B3);
  not not_219 (not_219_out, A3);
  not not_220 (not_220_out, B3);
  not not_221 (not_221_out, A3);
  not not_222 (not_222_out, B3);
  not not_223 (not_223_out, A3);
  not not_224 (not_224_out, B3);
  not not_225 (not_225_out, C_in);
  not not_226 (not_226_out, A2);
  not not_227 (not_227_out, A1);
  not not_228 (not_228_out, C_in);
  not not_229 (not_229_out, A2);
  not not_230 (not_230_out, B1);
  not not_231 (not_231_out, A2);
  not not_232 (not_232_out, A1);
  not not_233 (not_233_out, B1);
  not not_234 (not_234_out, A2);
  not not_235 (not_235_out, B2);
  not not_236 (not_236_out, C_in);
  not not_237 (not_237_out, A1);
  not not_238 (not_238_out, B2);
  not not_239 (not_239_out, C_in);
  not not_240 (not_240_out, B2);
  not not_241 (not_241_out, B1);
  not not_242 (not_242_out, A1);
  not not_243 (not_243_out, B2);
  not not_244 (not_244_out, B1);
  not not_245 (not_245_out, A2);
  not not_246 (not_246_out, B2);
  not not_247 (not_247_out, A2);
  not not_248 (not_248_out, B2);
  not not_249 (not_249_out, C_in);
  not not_250 (not_250_out, A1);
  not not_251 (not_251_out, C_in);
  not not_252 (not_252_out, B1);
  not not_253 (not_253_out, A1);
  not not_254 (not_254_out, B1);
  and and_1 (and_1_out, A1, B4, B3, B2, B1);
  and and_2 (and_2_out, A2, B4, B3, B2);
  and and_3 (and_3_out, A2, A1, B4, B3, B1);
  and and_4 (and_4_out, A3, B4, B3);
  and and_5 (and_5_out, A3, A1, B4, B2, B1);
  and and_6 (and_6_out, A3, A2, B4, B2);
  and and_7 (and_7_out, A3, A2, A1, B4, B1);
  and and_8 (and_8_out, A4, B4);
  and and_9 (and_9_out, A4, A1, B3, B2, B1);
  and and_10 (and_10_out, A4, A2, B3, B2);
  and and_11 (and_11_out, A4, A2, A1, B3, B1);
  and and_12 (and_12_out, A4, A3, B3);
  and and_13 (and_13_out, A4, A3, A1, B2, B1);
  and and_14 (and_14_out, A4, A3, A2, B2);
  and and_15 (and_15_out, A4, A3, A2, A1, B1);
  and and_16 (and_16_out, C_in, B4, B3, B2, B1);
  and and_17 (and_17_out, C_in, A1, B4, B3, B2);
  and and_18 (and_18_out, C_in, A2, B4, B3, B1);
  and and_19 (and_19_out, C_in, A2, A1, B4, B3);
  and and_20 (and_20_out, C_in, A3, B4, B2, B1);
  and and_21 (and_21_out, C_in, A3, A1, B4, B2);
  and and_22 (and_22_out, C_in, A3, A2, B4, B1);
  and and_23 (and_23_out, C_in, A3, A2, A1, B4);
  and and_24 (and_24_out, C_in, A4, B3, B2, B1);
  and and_25 (and_25_out, C_in, A4, A1, B3, B2);
  and and_26 (and_26_out, C_in, A4, A2, B3, B1);
  and and_27 (and_27_out, C_in, A4, A2, A1, B3);
  and and_28 (and_28_out, C_in, A4, A3, B2, B1);
  and and_29 (and_29_out, not_1_out, not_2_out, not_3_out, not_4_out, not_5_out, B4);
  and and_30 (and_30_out, not_6_out, not_7_out, not_8_out, not_9_out, B4, not_10_out);
  and and_31 (and_31_out, not_11_out, not_12_out, not_13_out, not_14_out, B4, not_15_out);
  and and_32 (and_32_out, not_16_out, not_17_out, not_18_out, B4, not_19_out, not_20_out);
  and and_33 (and_33_out, not_21_out, not_22_out, not_23_out, not_24_out, B4, not_25_out);
  and and_34 (and_34_out, not_26_out, not_27_out, not_28_out, B4, not_29_out, not_30_out);
  and and_35 (and_35_out, not_31_out, not_32_out, not_33_out, B4, not_34_out, not_35_out);
  and and_36 (and_36_out, not_36_out, not_37_out, B4, not_38_out, not_39_out, not_40_out);
  and and_37 (and_37_out, not_41_out, not_42_out, not_43_out, not_44_out, B4, not_45_out);
  and and_38 (and_38_out, not_46_out, not_47_out, not_48_out, B4, not_49_out);
  and and_39 (and_39_out, not_50_out, not_51_out, not_52_out, B4, not_53_out, not_54_out);
  and and_40 (and_40_out, not_55_out, not_56_out, B4, not_57_out);
  and and_41 (and_41_out, not_58_out, not_59_out, not_60_out, B4, not_61_out, not_62_out);
  and and_42 (and_42_out, not_63_out, not_64_out, B4, not_65_out, not_66_out);
  and and_43 (and_43_out, not_67_out, not_68_out, B4, not_69_out, not_70_out, not_71_out);
  and and_44 (and_44_out, not_72_out, A1, not_73_out, B3, B2, B1);
  and and_45 (and_45_out, not_74_out, A2, not_75_out, B3, B2);
  and and_46 (and_46_out, not_76_out, A2, A1, not_77_out, B3, B1);
  and and_47 (and_47_out, not_78_out, A3, not_79_out, B3);
  and and_48 (and_48_out, not_80_out, A3, A1, not_81_out, B2, B1);
  and and_49 (and_49_out, not_82_out, A3, A2, not_83_out, B2);
  and and_50 (and_50_out, not_84_out, A3, A2, A1, not_85_out, B1);
  and and_51 (and_51_out, not_86_out, A4, not_87_out, not_88_out, not_89_out, not_90_out);
  and and_52 (and_52_out, not_91_out, A4, not_92_out, not_93_out, not_94_out, not_95_out);
  and and_53 (and_53_out, not_96_out, A4, not_97_out, not_98_out, not_99_out, not_100_out);
  and and_54 (and_54_out, not_101_out, A4, not_102_out, not_103_out, not_104_out, not_105_out);
  and and_55 (and_55_out, not_106_out, A4, not_107_out, not_108_out, not_109_out, not_110_out);
  and and_56 (and_56_out, A4, not_111_out, not_112_out, not_113_out, not_114_out, not_115_out);
  and and_57 (and_57_out, A4, not_116_out, not_117_out, not_118_out, not_119_out);
  and and_58 (and_58_out, A4, not_120_out, not_121_out, not_122_out, not_123_out, not_124_out);
  and and_59 (and_59_out, A4, not_125_out, not_126_out, not_127_out);
  and and_60 (and_60_out, A4, not_128_out, not_129_out, not_130_out, not_131_out);
  and and_61 (and_61_out, A4, not_132_out, not_133_out, not_134_out, not_135_out);
  and and_62 (and_62_out, A4, not_136_out, not_137_out, not_138_out, not_139_out);
  and and_63 (and_63_out, A4, not_140_out, not_141_out, not_142_out, not_143_out);
  and and_64 (and_64_out, A4, A1, B4, B3, B2, B1);
  and and_65 (and_65_out, A4, A2, B4, B3, B2);
  and and_66 (and_66_out, A4, A2, A1, B4, B3, B1);
  and and_67 (and_67_out, A4, A3, B4, B3);
  and and_68 (and_68_out, A4, A3, A1, B4, B2, B1);
  and and_69 (and_69_out, A4, A3, A2, B4, B2);
  and and_70 (and_70_out, A4, A3, A2, A1, B4, B1);
  and and_71 (and_71_out, C_in, not_144_out, not_145_out, B3, B2, B1);
  and and_72 (and_72_out, C_in, not_146_out, A1, not_147_out, B3, B2);
  and and_73 (and_73_out, C_in, not_148_out, A2, not_149_out, B3, B1);
  and and_74 (and_74_out, C_in, not_150_out, A2, A1, not_151_out, B3);
  and and_75 (and_75_out, C_in, not_152_out, A3, not_153_out, B2, B1);
  and and_76 (and_76_out, C_in, A3, A1, not_154_out, B2);
  and and_77 (and_77_out, C_in, A3, A2, not_155_out, B1);
  and and_78 (and_78_out, C_in, A3, A2, A1, not_156_out);
  and and_79 (and_79_out, C_in, A4, B4, B3, B2, B1);
  and and_80 (and_80_out, C_in, A4, A1, B4, B3, B2);
  and and_81 (and_81_out, C_in, A4, A2, B4, B3, B1);
  and and_82 (and_82_out, C_in, A4, A2, A1, B4, B3);
  and and_83 (and_83_out, C_in, A4, A3, B4, B2, B1);
  and and_84 (and_84_out, not_157_out, not_158_out, not_159_out, not_160_out, B3);
  and and_85 (and_85_out, not_161_out, not_162_out, not_163_out, B3, not_164_out);
  and and_86 (and_86_out, not_165_out, not_166_out, not_167_out, B3, not_168_out);
  and and_87 (and_87_out, not_169_out, not_170_out, B3, not_171_out, not_172_out);
  and and_88 (and_88_out, not_173_out, not_174_out, not_175_out, B3, not_176_out);
  and and_89 (and_89_out, not_177_out, not_178_out, B3, not_179_out);
  and and_90 (and_90_out, not_180_out, not_181_out, B3, not_182_out, not_183_out);
  and and_91 (and_91_out, not_184_out, A1, not_185_out, B2, B1);
  and and_92 (and_92_out, not_186_out, A2, not_187_out, B2);
  and and_93 (and_93_out, not_188_out, A2, A1, not_189_out, B1);
  and and_94 (and_94_out, not_190_out, A3, not_191_out, not_192_out, not_193_out);
  and and_95 (and_95_out, not_194_out, A3, not_195_out, not_196_out, not_197_out);
  and and_96 (and_96_out, not_198_out, A3, not_199_out, not_200_out, not_201_out);
  and and_97 (and_97_out, not_202_out, A3, not_203_out, not_204_out, not_205_out);
  and and_98 (and_98_out, A3, not_206_out, not_207_out, not_208_out, not_209_out);
  and and_99 (and_99_out, A3, not_210_out, not_211_out, not_212_out);
  and and_100 (and_100_out, A3, not_213_out, not_214_out, not_215_out, not_216_out);
  and and_101 (and_101_out, A3, A1, B3, B2, B1);
  and and_102 (and_102_out, A3, A2, B3, B2);
  and and_103 (and_103_out, A3, A2, A1, B3, B1);
  and and_104 (and_104_out, C_in, not_217_out, not_218_out, B2, B1);
  and and_105 (and_105_out, C_in, not_219_out, A1, not_220_out, B2);
  and and_106 (and_106_out, C_in, not_221_out, A2, not_222_out, B1);
  and and_107 (and_107_out, C_in, not_223_out, A2, A1, not_224_out);
  and and_108 (and_108_out, C_in, A3, B3, B2, B1);
  and and_109 (and_109_out, C_in, A3, A1, B3, B2);
  and and_110 (and_110_out, C_in, A3, A2, B3, B1);
  and and_111 (and_111_out, C_in, A3, A2, A1, B3);
  and and_112 (and_112_out, not_225_out, not_226_out, not_227_out, B2);
  and and_113 (and_113_out, not_228_out, not_229_out, B2, not_230_out);
  and and_114 (and_114_out, not_231_out, not_232_out, B2, not_233_out);
  and and_115 (and_115_out, not_234_out, A1, not_235_out, B1);
  and and_116 (and_116_out, not_236_out, A2, not_237_out, not_238_out);
  and and_117 (and_117_out, not_239_out, A2, not_240_out, not_241_out);
  and and_118 (and_118_out, A2, not_242_out, not_243_out, not_244_out);
  and and_119 (and_119_out, A2, A1, B2, B1);
  and and_120 (and_120_out, C_in, not_245_out, not_246_out, B1);
  and and_121 (and_121_out, C_in, not_247_out, A1, not_248_out);
  and and_122 (and_122_out, C_in, A2, B2, B1);
  and and_123 (and_123_out, C_in, A2, A1, B2);
  and and_124 (and_124_out, not_249_out, not_250_out, B1);
  and and_125 (and_125_out, not_251_out, A1, not_252_out);
  and and_126 (and_126_out, C_in, not_253_out, not_254_out);
  and and_127 (and_127_out, C_in, A1, B1);
  or or_1 (Soma2, and_112_out, and_113_out, and_114_out, and_115_out, and_116_out, and_117_out, and_118_out, and_119_out, and_120_out, and_121_out, and_122_out, and_123_out);
  or or_2 (Soma1, and_124_out, and_125_out, and_126_out, and_127_out);
  or or_3 (C_out, and_1_out, and_2_out, and_3_out, and_4_out, and_5_out, and_6_out, and_7_out, and_8_out, and_9_out, and_10_out, and_11_out, and_12_out, and_13_out, and_14_out, and_15_out, and_16_out, and_17_out, and_18_out, and_19_out, and_20_out, and_21_out, and_22_out, and_23_out, and_24_out, and_25_out, and_26_out, and_27_out, and_28_out);
  or or_4 (or_4_out, and_29_out, and_30_out, and_31_out, and_32_out, and_33_out, and_34_out, and_35_out, and_36_out, and_37_out, and_38_out, and_39_out, and_40_out, and_41_out, and_42_out, and_43_out, and_44_out, and_45_out, and_46_out, and_47_out, and_48_out, and_49_out, and_50_out, and_51_out, and_52_out, and_53_out, and_54_out, and_55_out, and_56_out);
  or or_5 (or_5_out, and_57_out, and_58_out, and_59_out, and_60_out, and_61_out, and_62_out, and_63_out, and_64_out, and_65_out, and_66_out, and_67_out, and_68_out, and_69_out, and_70_out, and_71_out, and_72_out, and_73_out, and_74_out, and_75_out, and_76_out, and_77_out, and_78_out, and_79_out, and_80_out, and_81_out, and_82_out, and_83_out);
  or or_6 (Soma3, and_84_out, and_85_out, and_86_out, and_87_out, and_88_out, and_89_out, and_90_out, and_91_out, and_92_out, and_93_out, and_94_out, and_95_out, and_96_out, and_97_out, and_98_out, and_99_out, and_100_out, and_101_out, and_102_out, and_103_out, and_104_out, and_105_out, and_106_out, and_107_out, and_108_out, and_109_out, and_110_out, and_111_out);
  or or_7 (Soma4, or_4_out, or_5_out);
endmodule
