// Logisim project Somador de 4bits CLA com display.circ as structural Verilog: 1 circuit, main circuit main
module main (
  input  c0,
  input  [3:0] a,
  input  [3:0] b
);

  wire decodificador_4bits_para_display_7_segmentos_1_a, decodificador_4bits_para_display_7_segmentos_1_b,
       decodificador_4bits_para_display_7_segmentos_1_c, decodificador_4bits_para_display_7_segmentos_1_d,
       decodificador_4bits_para_display_7_segmentos_1_e, decodificador_4bits_para_display_7_segmentos_1_f,
       decodificador_4bits_para_display_7_segmentos_1_g, decodificador_4bits_para_display_7_segmentos_2_a,
       decodificador_4bits_para_display_7_segmentos_2_b, decodificador_4bits_para_display_7_segmentos_2_c,
       decodificador_4bits_para_display_7_segmentos_2_d, decodificador_4bits_para_display_7_segmentos_2_e,
       decodificador_4bits_para_display_7_segmentos_2_f, decodificador_4bits_para_display_7_segmentos_2_g,
       decodificador_4bits_para_display_7_segmentos_3_a, decodificador_4bits_para_display_7_segmentos_3_b,
       decodificador_4bits_para_display_7_segmentos_3_c, decodificador_4bits_para_display_7_segmentos_3_d,
       decodificador_4bits_para_display_7_segmentos_3_e, decodificador_4bits_para_display_7_segmentos_3_f,
       decodificador_4bits_para_display_7_segmentos_3_g;
  wire [3:0] main_1_soma1;

  Somador_de_4bits_CLA_main main_1 (
    .C0(c0), .A1(a[0]), .B1(b[0]), .A2(a[1]), .B2(b[1]), .A3(a[2]), .B3(b[2]), .A4(a[3]), .B4(b[3]),
    .Soma1(main_1_soma1[0]), .Soma2(main_1_soma1[1]), .Soma3(main_1_soma1[2]), .Soma4(main_1_soma1[3]));  // open: C4
  Decodificador_4bits_para_display_7_segmentos decodificador_4bits_para_display_7_segmentos_1 (
    .n1(a[0]), .n2(a[1]), .n3(a[2]), .n4(a[3]), .g(decodificador_4bits_para_display_7_segmentos_1_g),
    .f(decodificador_4bits_para_display_7_segmentos_1_f),
    .e(decodificador_4bits_para_display_7_segmentos_1_e),
    .d(decodificador_4bits_para_display_7_segmentos_1_d),
    .c(decodificador_4bits_para_display_7_segmentos_1_c),
    .b(decodificador_4bits_para_display_7_segmentos_1_b), .a(decodificador_4bits_para_display_7_segmentos_1_a));
  _7_Segment_Display u_7_segment_display_1 (
    .g(decodificador_4bits_para_display_7_segmentos_1_g),
    .f(decodificador_4bits_para_display_7_segmentos_1_f),
    .a(decodificador_4bits_para_display_7_segmentos_1_a),
    .b(decodificador_4bits_para_display_7_segmentos_1_b),
    .e(decodificador_4bits_para_display_7_segmentos_1_e),
    .d(decodificador_4bits_para_display_7_segmentos_1_d), .c(decodificador_4bits_para_display_7_segmentos_1_c));  // open: dp
  Decodificador_4bits_para_display_7_segmentos decodificador_4bits_para_display_7_segmentos_2 (
    .n1(b[0]), .n2(b[1]), .n3(b[2]), .n4(b[3]), .g(decodificador_4bits_para_display_7_segmentos_2_g),
    .f(decodificador_4bits_para_display_7_segmentos_2_f),
    .e(decodificador_4bits_para_display_7_segmentos_2_e),
    .d(decodificador_4bits_para_display_7_segmentos_2_d),
    .c(decodificador_4bits_para_display_7_segmentos_2_c),
    .b(decodificador_4bits_para_display_7_segmentos_2_b), .a(decodificador_4bits_para_display_7_segmentos_2_a));
  _7_Segment_Display u_7_segment_display_2 (
    .g(decodificador_4bits_para_display_7_segmentos_2_g),
    .f(decodificador_4bits_para_display_7_segmentos_2_f),
    .a(decodificador_4bits_para_display_7_segmentos_2_a),
    .b(decodificador_4bits_para_display_7_segmentos_2_b),
    .e(decodificador_4bits_para_display_7_segmentos_2_e),
    .d(decodificador_4bits_para_display_7_segmentos_2_d), .c(decodificador_4bits_para_display_7_segmentos_2_c));  // open: dp
  _7_Segment_Display u_7_segment_display_3 (
    .g(decodificador_4bits_para_display_7_segmentos_3_g),
    .f(decodificador_4bits_para_display_7_segmentos_3_f),
    .a(decodificador_4bits_para_display_7_segmentos_3_a),
    .b(decodificador_4bits_para_display_7_segmentos_3_b),
    .e(decodificador_4bits_para_display_7_segmentos_3_e),
    .d(decodificador_4bits_para_display_7_segmentos_3_d), .c(decodificador_4bits_para_display_7_segmentos_3_c));  // open: dp
  Decodificador_4bits_para_display_7_segmentos decodificador_4bits_para_display_7_segmentos_3 (
    .n1(main_1_soma1[0]), .n2(main_1_soma1[1]), .n3(main_1_soma1[2]), .n4(main_1_soma1[3]),
    .g(decodificador_4bits_para_display_7_segmentos_3_g),
    .f(decodificador_4bits_para_display_7_segmentos_3_f),
    .e(decodificador_4bits_para_display_7_segmentos_3_e),
    .d(decodificador_4bits_para_display_7_segmentos_3_d),
    .c(decodificador_4bits_para_display_7_segmentos_3_c),
    .b(decodificador_4bits_para_display_7_segmentos_3_b), .a(decodificador_4bits_para_display_7_segmentos_3_a));

  // Notes on the sheet:
  //   +
  //   =
endmodule
