// Logisim project Somador de 4bits CLA.circ as structural Verilog: 1 circuit, main circuit main
module main (
  input  C0,
  input  A1,
  input  B1,
  input  A2,
  input  B2,
  input  A3,
  input  B3,
  input  A4,
  input  B4,
  output Soma1,
  output Soma2,
  output Soma3,
  output Soma4,
  output C4
);

  wire and_1_out, and_2_out, and_3_out, and_4_out, and_5_out, and_6_out, and_7_out, and_8_out, and_9_out,
       and_10_out, and_11_out, and_12_out, and_13_out, and_14_out, buffer_1_out, buffer_2_out, buffer_3_out,
       buffer_4_out, nand_1_out, nand_2_out, nand_3_out, nand_4_out, nor_1_out, nor_2_out, nor_3_out,
       nor_4_out, nor_5_out, nor_6_out, nor_7_out, not_1_out, not_2_out;

  not not_1 (not_1_out, C0);
  nor nor_1 (nor_1_out, A1, B1);
  not not_2 (not_2_out, not_1_out);
  xor xor_1 (Soma1, not_2_out, and_1_out);
  nand nand_1 (nand_1_out, A1, B1);
  and and_1 (and_1_out, ~nor_1_out, nand_1_out);  // AND_Gate
  and and_2 (and_2_out, not_1_out, nand_1_out);
  nor nor_2 (nor_2_out, A2, B2);
  buf buffer_1 (buffer_1_out, nor_1_out);
  nor nor_3 (nor_3_out, and_2_out, buffer_1_out);
  xor xor_2 (Soma2, nor_3_out, and_3_out);
  nand nand_2 (nand_2_out, A2, B2);
  and and_3 (and_3_out, ~nor_2_out, nand_2_out);  // AND_Gate
  and and_4 (and_4_out, nand_2_out, nor_1_out);
  and and_5 (and_5_out, not_1_out, nand_1_out, nand_2_out);
  nor nor_4 (nor_4_out, and_5_out, and_4_out, buffer_2_out);
  nor nor_5 (nor_5_out, A3, B3);
  buf buffer_2 (buffer_2_out, nor_2_out);
  xor xor_3 (Soma3, nor_4_out, and_6_out);
  nand nand_3 (nand_3_out, A3, B3);
  and and_6 (and_6_out, ~nor_5_out, nand_3_out);  // AND_Gate
  and and_7 (and_7_out, not_1_out, nand_1_out, nand_2_out, nand_3_out);
  and and_8 (and_8_out, nand_2_out, nand_3_out, nor_1_out);
  nor nor_6 (nor_6_out, and_7_out, and_8_out, and_9_out, buffer_3_out);
  buf buffer_3 (buffer_3_out, nor_5_out);
  and and_9 (and_9_out, nand_3_out, nor_2_out);
  xor xor_4 (Soma4, nor_6_out, and_10_out);
  nor nor_7 (nor_7_out, A4, B4);
  nand nand_4 (nand_4_out, A4, B4);
  and and_10 (and_10_out, ~nor_7_out, nand_4_out);  // AND_Gate
  and and_11 (and_11_out, not_1_out, nand_1_out, nand_2_out, nand_3_out, nand_4_out);
  and and_12 (and_12_out, nand_3_out, nand_4_out, nor_2_out);
  and and_13 (and_13_out, nand_2_out, nand_3_out, nand_4_out, nor_1_out);
  nor nor_8 (C4, and_11_out, and_13_out, and_12_out, and_14_out, buffer_4_out);
  buf buffer_4 (buffer_4_out, nor_7_out);
  and and_14 (and_14_out, nand_4_out, nor_5_out);
endmodule
