// Logisim project Somador_completo_a_mais_b_mais_bit_recebido.circ as structural Verilog: 1 circuit, main circuit main
module main (
  input  a,
  input  b,
  input  received,
  output send_bit,
  output bit0
);

  wire half_adder_3_send_bit, half_adder_bit0, half_adder_send_bit;

  Meio_somador_main half_adder (.a(b), .b(a), .send_bit(half_adder_send_bit), .bit0(half_adder_bit0));
  Meio_somador_main half_adder_2 (
    .a(half_adder_3_send_bit), .b(half_adder_send_bit), .bit0(send_bit));  // open: send_bit
  Meio_somador_main half_adder_3 (.a(received), .b(half_adder_bit0), .send_bit(half_adder_3_send_bit), .bit0(bit0));

  // Notes on the sheet:
  //   a + b + received = send_bit  bit0
  //   0 + 0 +           0  = 0               0
  //   0 + 1 +           0  = 0               1
  //   1 + 0 +           0  = 0               1
  //   1 + 1 +           0  = 1               0
  //   0 + 0 +           1  = 0               1
  //   0 + 1 +           1  = 1               0
  //   1 + 0 +           1  = 1               0
  //   1 + 1 +           1  = 1               1
endmodule
