// Logisim project ULA 1bit (and, or, not, sum, subtract).circ as structural Verilog: 1 circuit, main circuit main
module main (
  input  b_invert,
  input  carry_in,
  input  a,
  input  b,
  input  [1:0] op_code,
  output carry_out,
  output result
);

  wire and_1_out, main_1_bit0, multiplexer_1_out, not_1_out, not_2_out, or_1_out;

  not not_1 (not_1_out, b);
  Multiplexer #(.enable("false")) multiplexer_1 (.in0(b), .in1(not_1_out), .out(multiplexer_1_out), .sel(b_invert));
  and and_1 (and_1_out, a, b);
  or or_1 (or_1_out, a, b);
  not not_2 (not_2_out, a);
  Somador_completo_a_mais_b_mais_bit_recebido_main main_1 (
    .a(a), .b(multiplexer_1_out), .received(carry_in), .send_bit(carry_out), .bit0(main_1_bit0));
  Multiplexer #(.select(2), .enable("false")) multiplexer_2 (
    .in0(and_1_out), .in1(or_1_out), .in2(not_2_out), .in3(main_1_bit0), .out(result), .sel(op_code));

  // Notes on the sheet:
  //   op code -> op
  //   00 -> and(a, b)
  //   01 -> or(a, b)
  //   10 -> not(a)
  //   11 -> a + b
endmodule
